// Logisim project zdw9.circ as structural Verilog: 6 circuits, main circuit main
module main (
);

  wire and_1_out, and_2_out, CLK, clr, DEC7, flag, HALT, INC7, Itype, kbRE, looping, lpm, MemSelSrc, MemWE,
       Neg, not_1_out, not_2_out, not_3_out, or_1_out, or_2_out, out, outm, pause, PC_minusout, PC_zeroout,
       ProdSel, ProdWE, put, RegWE, stage, ttyWE, WReg, Zero;
  wire [1:0] MemAddSel;
  wire [2:0] ALUOp, rd, RegSelSrc, rs, rt;
  wire [3:0] display_1_digit_0, display_1_digit_1, display_1_digit_2, display_1_digit_3, pcSelect;
  wire [6:0] kbOut, ttyIn;
  wire [15:0] adder_1_out, adder_2_out, aluOut, bit_extender_1_out, count, High, imm, instrIn,
       multiplexer_3_out, multiplexer_4_out, next, PCout, R, RAMaddr, RAMin, RAMout, Reg, RegIn, romIn,
       rsOut, rtOut, savedInstr, sp, subtractor_1_out, subtractor_2_out;
  wire [31:0] adder_3_out, multiplexer_8_out, ProdOut;

  Clock clock_1 (.out(CLK));
  LED u_HALT (.in(HALT));
  Hex_Digit_Display hex_digit_display_1 (.value(display_1_digit_3));  // open: dp
  Hex_Digit_Display hex_digit_display_2 (.value(display_1_digit_2));  // open: dp
  Display display_1 (
    .Data(rsOut), .Clock(CLK), .Write_Enable(put), .Clear(clr), .Digit_0(display_1_digit_0),
    .Digit_1(display_1_digit_1), .Digit_2(display_1_digit_2), .Digit_3(display_1_digit_3));
  PC_Control PC (
    .HALT(HALT), .PC_out(PCout), .Target(rsOut), .PcOpCode(pcSelect), .Clock(CLK), .MinusIn(Neg),
    .FLAG(flag), .zeroOut(PC_zeroout), .minusOut(PC_minusout), .Immediate(imm), .ZeroIn(Zero),
    .RAM_r7(RAMout), .pause(pause));
  Register_File register_file_1 (
    .ITYPE(Itype), .CLK(CLK), .DATA(RegIn), .WE(RegWE), .incr7(INC7), .decr7(DEC7), .rd(rd), .rs(rs),
    .rt(rt), .rt_out(rtOut), .rs_out(rsOut), .sp_out(sp));
  TTY tty_1 (.data(ttyIn), .clk(CLK), .we(ttyWE));  // open: clr
  Multiplexer #(.width(16), .enable("false")) multiplexer_1 (.in0(Reg), .in1(adder_1_out), .out(R), .sel(looping));
  Adder #(.width(16)) adder_1 (.a(rsOut), .b(16'h1), .out(adder_1_out));  // open: cin, cout
  Multiplexer #(.width(16), .enable("false")) multiplexer_2 (.in0(R), .in1(next), .out(RegIn), .sel(stage));
  Subtractor #(.width(16)) subtractor_1 (.a(count), .b(16'h1), .out(subtractor_1_out));  // open: bin, bout
  Hex_Digit_Display hex_digit_display_3 (.value(display_1_digit_1));  // open: dp
  Hex_Digit_Display hex_digit_display_4 (.value(display_1_digit_0));  // open: dp
  LED Negative (.in(PC_minusout));
  LED u_Zero (.in(PC_zeroout));
  Multiplexer #(.width(16), .enable("false")) multiplexer_3 (
    .in0(rtOut), .in1(subtractor_1_out), .out(multiplexer_3_out), .sel(looping));
  Register #(.width(16)) u_Count (.D(multiplexer_3_out), .en(or_1_out), .Q(count), .clk(CLK));  // open: clr
  or or_1 (or_1_out, outm, looping);
  Multiplexer #(.width(16), .enable("false")) multiplexer_4 (
    .in0(rtOut), .in1(imm), .out(multiplexer_4_out), .sel(Itype));
  Multiplexer #(.select(3), .width(16), .enable("false")) multiplexer_5 (
    .in0(aluOut), .in1(imm), .in2(RAMout), .in3(rsOut), .in4(ProdOut[15:0]), .in5(ProdOut[31:16]),
    .in6({imm[15:8], rsOut[7:0]}), .in7(bit_extender_1_out), .out(Reg), .sel(RegSelSrc));
  assign bit_extender_1_out = {{9{1'b0}}, kbOut};  // Bit_Extender bit_extender_1
  Multiplexer #(.width(16), .enable("false")) multiplexer_6 (
    .in0(next), .in1(savedInstr), .out(instrIn), .sel(or_2_out));
  or or_2 (or_2_out, and_1_out, looping);
  and and_1 (and_1_out, stage, lpm);
  ALU alu_1 (
    .OpCode(ALUOp), .A(rsOut), .B(multiplexer_4_out), .Result(aluOut), .High(High), .Zero(Zero),
    .Negative(Neg));
  Keyboard keyboard_1 (.clk(CLK), .re(kbRE), .data(kbOut));  // open: clr, avail
  ROM #(.addrWidth(16), .dataWidth(16)) rom_1 (.addr(romIn), .data(next));  // open: sel
  Multiplexer #(.width(16), .enable("false")) multiplexer_7 (
    .in0(rtOut), .in1(adder_2_out), .out(RAMin), .sel(MemSelSrc));
  Adder #(.width(16)) adder_2 (.a(PCout), .b(16'h1), .out(adder_2_out));  // open: cin, cout
  not not_1 (not_1_out, stage);
  not not_2 (not_2_out, stage);
  and and_2 (and_2_out, not_2_out, lpm);
  Comparator #(.width(16)) comparator_1 (.a(count), .b({16{1'b0}}), .gt(looping));  // open: eq, lt
  Register #(.width(16), .trigger("falling")) Saved_Instruction (
    .D(next), .en(not_1_out), .Q(savedInstr), .clk(CLK));  // open: clr
  or or_3 (pause, and_2_out, outm, looping);
  Main_Control main_control_1 (
    .Instruction(instrIn), .rd(rd), .rs(rs), .rt(rt), .Immediate(imm), .IType(Itype), .MemWE(MemWE),
    .HALT(HALT), .RegWE(WReg), .INC7(INC7), .DEC7(DEC7), .CLEAR(clr), .PUT(put), .ALUOp(ALUOp),
    .pcOp(pcSelect), .flag(flag), .ProdWE(ProdWE), .ProdSelect(ProdSel), .MemDataSrc(MemSelSrc),
    .regSelSrc(RegSelSrc), .MemAddSrc(MemAddSel), .kbRE(kbRE), .out(out), .lpm(lpm), .outm(outm));
  Subtractor #(.width(16)) subtractor_2 (.a(sp), .b(16'h1), .out(subtractor_2_out));  // open: bin, bout
  not not_3 (not_3_out, stage);
  RAM #(.addrWidth(16), .dataWidth(16), .bus("separate")) ram_1 (
    .addr(RAMaddr), .din(RAMin), .data(RAMout), .str(MemWE), .clk(CLK));  // open: sel, ld, clr
  Register #(.width(32)) Product (.D(multiplexer_8_out), .en(ProdWE), .Q(ProdOut), .clk(CLK));  // open: clr
  Multiplexer #(.width(32), .enable("false")) multiplexer_8 (
    .in0({High, aluOut}), .in1(adder_3_out), .out(multiplexer_8_out), .sel(ProdSel));
  Adder #(.width(32)) adder_3 (.a({High, aluOut}), .b(ProdOut), .out(adder_3_out));  // open: cin, cout
  Multiplexer #(.select(2), .width(16), .enable("false")) multiplexer_9 (
    .in0(rsOut), .in1(sp), .in2(subtractor_2_out), .out(RAMaddr), .sel(MemAddSel));  // open: in3
  Register #(.width(1), .trigger("falling")) lpmStage (.D(not_3_out), .en(lpm), .Q(stage), .clk(CLK));  // open: clr
  or or_4 (RegWE, WReg, looping, stage);
  Multiplexer #(.width(16), .enable("false")) multiplexer_10 (.in0(PCout), .in1(rsOut), .out(romIn), .sel(stage));
  or or_5 (ttyWE, out, looping);
  Multiplexer #(.width(7), .enable("false")) multiplexer_11 (
    .in0(rsOut[6:0]), .in1(RAMout[6:0]), .out(ttyIn), .sel(looping));

  // Notes on the sheet:
  //   CS 447 MWF 11AM
  //   Zachary Whitney Project 2
endmodule

// DISPLAY
module Display (
  input  [15:0] Data,
  input  Clock,
  input  Write_Enable,
  input  Clear,
  output [3:0] Digit_0,
  output [3:0] Digit_1,
  output [3:0] Digit_2,
  output [3:0] Digit_3
);

  wire or_1_out;
  wire [15:0] multiplexer_1_out;

  Multiplexer #(.width(16), .enable("false")) multiplexer_1 (
    .in0(Data), .in1({16{1'b0}}), .out(multiplexer_1_out), .sel(Clear));
  or or_1 (or_1_out, Write_Enable, Clear);
  Register #(.width(16)) Stored_Value (
    .D(multiplexer_1_out), .en(or_1_out), .Q({Digit_3, Digit_2, Digit_1, Digit_0}), .clk(Clock));  // open: clr

  // Other names for the same wires on the sheet: CLK = Clock; CLR = Clear; WE = Write_Enable
endmodule

module ALU (
  input  [2:0] OpCode,
  input  [15:0] A,
  input  [15:0] B,
  output [15:0] Result,
  output [15:0] High,
  output Zero,
  output Negative
);

  wire [15:0] AND, Difference, not_1_out, notA, OR, Product, SLL, SRL, Sum;

  Adder #(.width(16)) adder_1 (.a(A), .b(B), .out(Sum));  // open: cin, cout
  Multiplier #(.width(16)) multiplier_1 (.a(A), .b(B), .out(Product), .cout(High));  // open: cin
  Shifter #(.width(16), .shift("lr")) shifter_1 (.in(A), .\dist (B[3:0]), .out(SRL));
  Shifter #(.width(16)) shifter_2 (.in(A), .\dist (B[3:0]), .out(SLL));
  Comparator #(.width(16)) comparator_1 (.a(Result), .b({16{1'b0}}), .eq(Zero), .lt(Negative));  // open: gt
  assign not_1_out = ~B;  // NOT_Gate not_1, 16 bits wide
  Adder #(.width(16)) adder_2 (.a(A), .b(not_1_out), .out(Difference), .cin(1'b1));  // open: cout
  assign notA = ~A;  // NOT_Gate not_2, 16 bits wide
  assign OR = A | B;  // OR_Gate or_1, 16 bits wide
  assign AND = A & B;  // AND_Gate and_1, 16 bits wide
  Multiplexer #(.select(3), .width(16), .enable("false")) multiplexer_1 (
    .in0(Sum), .in1(Difference), .in2(Product), .in3(AND), .in4(OR), .in5(notA), .in6(SLL), .in7(SRL),
    .out(Result), .sel(OpCode));
  // Probe on A
  // Probe on B
  // Probe on Result
  // Probe on High
  // Probe on Result

  // Other names for the same wires on the sheet: bLoBits[3:0] = B[3:0]; OP[2:0] = OpCode; Out[15:0] = Result
endmodule

module Register_File (
  input  ITYPE,
  input  CLK,
  input  [15:0] DATA,
  input  WE,
  input  incr7,
  input  decr7,
  input  [2:0] rd,
  input  [2:0] rs,
  input  [2:0] rt,
  output [15:0] rt_out,
  output [15:0] rs_out,
  output [15:0] sp_out
);

  wire _0e, _1e, _2e, _3e, _4e, _5e, _6e, _7e, adj, or_2_out;
  wire [2:0] rsSrc;
  wire [15:0] adder_1_out, multiplexer_4_out, r0out, r1out, r2out, r3out, r4out, r5out, r6out, r7in, r7temp,
       subtractor_1_out;

  Register #(.width(16)) r0 (.D(DATA), .en(_0e), .Q(r0out), .clk(CLK));  // open: clr
  Register #(.width(16)) r4 (.D(DATA), .en(_4e), .Q(r4out), .clk(CLK));  // open: clr
  or or_1 (adj, decr7, incr7);
  Register #(.width(16)) r1 (.D(DATA), .en(_1e), .Q(r1out), .clk(CLK));  // open: clr
  Register #(.width(16)) r5 (.D(DATA), .en(_5e), .Q(r5out), .clk(CLK));  // open: clr
  Multiplexer #(.select(3), .width(16), .enable("false")) multiplexer_1 (
    .in0(r0out), .in1(r1out), .in2(r2out), .in3(r3out), .in4(r4out), .in5(r5out), .in6(r6out), .in7(sp_out),
    .out(rt_out), .sel(rt));
  Multiplexer #(.width(3), .enable("false")) multiplexer_2 (.in0(rs), .in1(rd), .out(rsSrc), .sel(ITYPE));
  Register #(.width(16)) r2 (.D(DATA), .en(_2e), .Q(r2out), .clk(CLK));  // open: clr
  Register #(.width(16)) r6 (.D(DATA), .en(_6e), .Q(r6out), .clk(CLK));  // open: clr
  Multiplexer #(.select(3), .width(16), .enable("false")) multiplexer_3 (
    .in0(r0out), .in1(r1out), .in2(r2out), .in3(r3out), .in4(r4out), .in5(r5out), .in6(r6out), .in7(sp_out),
    .out(rs_out), .sel(rsSrc));
  Register #(.width(16)) r3 (.D(DATA), .en(_3e), .Q(r3out), .clk(CLK));  // open: clr
  Demultiplexer #(.select(3), .enable("false")) demultiplexer_1 (
    .out0(_0e), .out1(_1e), .out2(_2e), .out3(_3e), .out4(_4e), .out5(_5e), .out6(_6e), .out7(_7e), .in(WE),
    .sel(rd));
  Multiplexer #(.width(16), .enable("false")) multiplexer_4 (
    .in0(DATA), .in1(r7in), .out(multiplexer_4_out), .sel(adj));
  Register #(.width(16)) r7 (.D(multiplexer_4_out), .en(or_2_out), .Q(r7temp), .clk(CLK));  // open: clr
  or or_2 (or_2_out, _7e, incr7, decr7);
  Subtractor #(.width(16)) subtractor_1 (.a(r7temp), .b(16'h1), .out(subtractor_1_out));  // open: bin, bout
  Adder #(.width(16)) adder_1 (.a(sp_out), .b(16'h1), .out(adder_1_out));  // open: cin, cout
  Multiplexer #(.width(16), .enable("false")) multiplexer_5 (
    .in0(r7temp), .in1(subtractor_1_out), .out(sp_out), .sel(decr7));
  Multiplexer #(.width(16), .enable("false")) multiplexer_6 (.in0(sp_out), .in1(adder_1_out), .out(r7in), .sel(incr7));

  // Other names for the same wires on the sheet: I = ITYPE; r7out[15:0] = sp_out
endmodule

module PC_Control (
  input  [3:0] PcOpCode,
  input  FLAG,
  input  Clock,
  input  [15:0] Immediate,
  input  ZeroIn,
  input  [15:0] Target,
  input  [15:0] RAM_r7,
  input  MinusIn,
  input  HALT,
  input  pause,
  output zeroOut,
  output minusOut,
  output [15:0] PC_out
);

  wire and_1_out, and_2_out, and_3_out, and_4_out, and_5_out, and_6_out, b, beq, bez, bge, blt, bne, bnz,
       branch, call, jr, next, not_1_out, or_1_out, rdZero, ret;
  wire [1:0] pcDataSel;
  wire [15:0] adder_1_out, adder_2_out, PC_In;

  Decoder #(.select(4), .enable("false")) decoder_1 (
    .out0(next), .out1(b), .out2(jr), .out3(blt), .out4(bge), .out5(beq), .out6(bne), .out7(bez), .out8(bnz),
    .out9(call), .out10(ret), .sel(PcOpCode));  // open: out11, out12, out13, out14, out15
  Comparator #(.width(16)) comparator_1 (.a(Target), .b({16{1'b0}}), .eq(rdZero));  // open: gt, lt
  or or_1 (or_1_out, b, call);
  Register #(.width(16)) PC (.D(PC_In), .en(not_1_out), .Q(PC_out), .clk(Clock));  // open: clr
  not not_1 (not_1_out, HALT);
  and and_1 (and_1_out, bez, rdZero);
  and and_2 (and_2_out, beq, zeroOut);
  and and_3 (and_3_out, bnz, ~rdZero);  // AND_Gate
  and and_4 (and_4_out, blt, minusOut);
  and and_5 (and_5_out, bge, ~minusOut);  // AND_Gate
  and and_6 (and_6_out, bne, ~zeroOut);  // AND_Gate
  or or_2 (branch, and_2_out, and_1_out, and_3_out, or_1_out, and_4_out, and_5_out, and_6_out);
  Register #(.width(1)) Zero (.D(ZeroIn), .en(FLAG), .Q(zeroOut), .clk(Clock));  // open: clr
  Adder #(.width(16)) adder_1 (.a(PC_out), .b(16'h1), .out(adder_1_out));  // open: cin, cout
  Adder #(.width(16)) adder_2 (.a(adder_1_out), .b(Immediate), .out(adder_2_out));  // open: cin, cout
  Priority_Encoder #(.select(2)) priority_encoder_1 (
    .in0(1'b1), .in1(branch), .in2(jr), .in3(ret), .out(pcDataSel));  // open: gs, en_out, en_in
  Register #(.width(1)) Negative (.D(MinusIn), .en(FLAG), .Q(minusOut), .clk(Clock));  // open: clr
  Multiplexer #(.select(2), .width(16), .enable("false")) multiplexer_1 (
    .in0(adder_1_out), .in1(adder_2_out), .in2(Target), .in3(RAM_r7), .out(PC_In), .sel(pcDataSel));

  // Other names for the same wires on the sheet: CLK = Clock; CurrPC[15:0] = PC_out; op[3:0] = PcOpCode;
  //   sp[15:0] = RAM_r7
endmodule

module Main_Control (
  input  [15:0] Instruction,
  output [2:0] rd,
  output [2:0] rs,
  output [2:0] rt,
  output [15:0] Immediate,
  output IType,
  output MemWE,
  output HALT,
  output RegWE,
  output INC7,
  output DEC7,
  output CLEAR,
  output PUT,
  output [2:0] ALUOp,
  output MemDataSrc,
  output [3:0] pcOp,
  output flag,
  output ProdWE,
  output [1:0] MemAddSrc,
  output ProdSelect,
  output [2:0] regSelSrc,
  output kbRE,
  output out,
  output lpm,
  output outm
);

  wire _4bits, add, adi, \and , ani, b, beq, bez, bge, blt, bne, bnz, call, cmp, cpi, jr, ld, li, lui, mfhi,
       mflo, mov, mul, \not , \or , or_1_out, or_4_out, or_5_out, or_6_out, or_7_out, or_8_out, or_9_out,
       or_10_out, ori, pop, push, ret, shl, shr, sli, sri, st, sub, zxt;
  wire [1:0] immSel;
  wire [4:0] multiplexer_1_out, multiplexer_2_out;
  wire [15:0] bit_extender_1_out, bit_extender_2_out, bit_extender_3_out;

  Decoder #(.select(5)) decoder_1 (
    .out16(li), .out17(lui), .out18(adi), .out19(ani), .out20(ori), .out21(sli), .out22(sri), .out23(cpi),
    .out24(b), .out25(blt), .out26(bge), .out27(beq), .out28(bne), .out29(bez), .out30(bnz), .out31(call),
    .sel(multiplexer_1_out));  // open: out0, out1, out2, out3, out4, out5, out6, out7, out8, out9, out10, out11, out12, out13, out14, out15, en
  Multiplexer #(.width(5), .enable("false")) multiplexer_1 (
    .in0({5{1'b0}}), .in1(Instruction[15:11]), .out(multiplexer_1_out), .sel(Instruction[15]));
  Decoder #(.select(5)) decoder_2 (
    .out0(HALT), .out1(PUT), .out2(CLEAR), .out3(mov), .out4(mfhi), .out5(mflo), .out6(ld), .out7(st),
    .out8(push), .out9(pop), .out10(add), .out11(sub), .out12(cmp), .out13(mul), .out14(ProdSelect),
    .out15(\and ), .out16(\or ), .out17(\not ), .out18(shl), .out19(shr), .out20(jr), .out21(ret),
    .out22(kbRE), .out23(out), .out24(lpm), .out25(outm), .sel(multiplexer_2_out));  // open: out26, out27, out28, out29, out30, out31, en
  Multiplexer #(.width(5), .enable("false")) multiplexer_2 (
    .in0(Instruction[13:9]), .in1({5{1'b1}}), .out(multiplexer_2_out), .sel(Instruction[15]));
  Priority_Encoder #(.select(1)) priority_encoder_1 (
    .in0(1'b1), .in1(call), .out(MemDataSrc));  // open: gs, en_out, en_in
  or or_1 (or_1_out, push, ret, pop, call);
  or or_2 (MemWE, st, push, call);
  or or_3 (INC7, pop, ret);
  or or_4 (or_4_out, sub, cpi, cmp);
  or or_5 (or_5_out, ProdSelect, mul);
  or or_6 (or_6_out, \and , ani);
  or or_7 (or_7_out, \or , ori);
  or or_8 (or_8_out, shl, sli);
  or or_9 (or_9_out, shr, sri);
  Priority_Encoder #(.select(2)) priority_encoder_2 (
    .in0(1'b1), .in1(or_1_out), .out(MemAddSrc));  // open: in2, in3, gs, en_out, en_in
  assign bit_extender_1_out = {{8{Instruction[10]}}, Instruction[10:3]};  // Bit_Extender bit_extender_1
  assign bit_extender_2_out = {{8{1'b0}}, Instruction[10:3]};  // Bit_Extender bit_extender_2
  assign bit_extender_3_out = {{12{1'b0}}, Instruction[6:3]};  // Bit_Extender bit_extender_3
  or or_10 (or_10_out, ld, pop);
  Priority_Encoder priority_encoder_3 (
    .in0(1'b1), .in1(or_4_out), .in2(or_5_out), .in3(or_6_out), .in4(or_7_out), .in5(\not ), .in6(or_8_out),
    .in7(or_9_out), .out(ALUOp));  // open: en_in, gs, en_out
  Multiplexer #(.select(2), .width(16), .enable("false")) multiplexer_3 (
    .in0(bit_extender_1_out), .in1(bit_extender_2_out), .in2({Instruction[10:3], {8{1'b0}}}),
    .in3(bit_extender_3_out), .out(Immediate), .sel(immSel));
  or or_11 (ProdWE, mul, ProdSelect);
  or or_12 (DEC7, push, call);
  Priority_Encoder #(.select(2)) priority_encoder_4 (
    .in0(1'b1), .in1(zxt), .in2(lui), .in3(_4bits), .out(immSel));  // open: gs, en_out, en_in
  or or_13 (_4bits, sri, sli);
  Priority_Encoder priority_encoder_5 (
    .in0(1'b1), .in1(li), .in2(or_10_out), .in3(mov), .in4(mflo), .in5(mfhi), .in6(lui), .in7(kbRE),
    .out(regSelSrc));  // open: en_in, gs, en_out
  Priority_Encoder #(.select(4)) priority_encoder_6 (
    .in0(1'b1), .in1(b), .in2(jr), .in3(blt), .in4(bge), .in5(beq), .in6(bne), .in7(bez), .in8(bnz),
    .in9(call), .in10(ret), .out(pcOp));  // open: in11, in12, in13, in14, in15, gs, en_out, en_in
  or or_14 (RegWE, \and , li, lui, mov, mfhi, mflo, ld, pop, add, sub, \or , \not , shl, shr, adi, ani, ori, sli, sri, kbRE);
  or or_15 (zxt, li, ani, ori);
  or or_16 (flag, cpi, adi, add, sub, cmp);

  assign IType = Instruction[15];
  assign rd = Instruction[2:0];
  assign rs = Instruction[8:6];
  assign rt = Instruction[5:3];

  // Other names for the same wires on the sheet: INPUT[15:0] = Instruction; ROpCode[5:0] = Instruction[14:9];
  //   clr = CLEAR; imm[15:0] = Immediate; in = kbRE; IOpCode[4:0] = Instruction[15:11]; mac = ProdSelect
endmodule
