// Logisim project constant_gates.circ as structural Verilog: 1 circuit, main circuit main
module main (
  input  in_1,
  input  in_2,
  input  in_3
);

  wire and_1_out, and_2_out, or_1_out, or_2_out, xor_1_out, xor_2_out;

  // Probe on and_1_out
  and and_1 (and_1_out, in_1, 1'b0);
  // Probe on or_1_out
  or or_1 (or_1_out, in_1, 1'b1);
  and and_2 (and_2_out, in_2, 1'b1);
  // Probe on and_2_out
  or or_2 (or_2_out, in_2, 1'b0);
  // Probe on or_2_out
  // Probe on xor_1_out
  xor xor_1 (xor_1_out, in_2, 1'b0);
  // Probe on xor_2_out
  xor xor_2 (xor_2_out, in_3, 1'b1);

  // Notes on the sheet:
  //   These can be replaced with constants.
  //   These do nothing.
  //   This is the same as a NOT.
endmodule
