// Logisim project simple_counter.circ as structural Verilog: 1 circuit, main circuit main
module main (
);

  wire clock_1_out;
  wire [7:0] adder_1_out, register_1_q;

  Clock clock_1 (.out(clock_1_out));
  Register register_1 (.D(adder_1_out), .Q(register_1_q), .clk(clock_1_out));  // open: en, clr
  Adder adder_1 (.a(register_1_q), .b(8'h1), .out(adder_1_out));  // open: cin, cout

  // Notes on the sheet:
  //   When the clock ticks, the register counts up 1.
  //   This works because there's a delay between
  //   the time the register stores its value and the
  //   time a newly-calculated value arrives at its input.
endmodule
