// Logisim project zdw9_lab5.circ as structural Verilog: 1 circuit, main circuit main
module main (
  input  [7:0] A,
  input  [7:0] B,
  input  [1:0] Op,
  output [7:0] Out
);

  wire [7:0] adder_1_out, divider_1_out, multiplier_1_out, subtractor_1_out;

  // Probe on A
  // Probe on B
  Adder adder_1 (.a(A), .b(B), .out(adder_1_out));  // open: cin, cout
  Subtractor subtractor_1 (.a(A), .b(B), .out(subtractor_1_out));  // open: bin, bout
  Multiplier multiplier_1 (.a(A), .b(B), .out(multiplier_1_out));  // open: cin, cout
  Divider divider_1 (.a(A), .b(B), .out(divider_1_out));  // open: upper, rem
  Multiplexer #(.select(2), .width(8), .enable("false")) multiplexer_1 (
    .in0(adder_1_out), .in1(subtractor_1_out), .in2(multiplier_1_out), .in3(divider_1_out), .out(Out),
    .sel(Op));
  // Probe on Out

  // Notes on the sheet:
  //   Zachary Whitney Lab 5
  //   CS 447 MWF 11AM
endmodule
