// Logisim project zdw9_lab6.circ as structural Verilog: 2 circuits, main circuit main
module main (
);

  wire CLK, kOut, not_1_out;
  wire [3:0] adder_1_out, Counter_q;
  wire [7:0] _0s_q, _1s_q, adder_2_out, adder_3_out;

  Register #(.width(4)) Counter (.D(adder_1_out), .Q(Counter_q), .clk(CLK));  // open: en, clr
  Clock clock_1 (.out(CLK));
  Adder #(.width(4)) adder_1 (.a(Counter_q), .b(4'b0001), .out(adder_1_out));  // open: cin, cout
  kmap kmap (.A(Counter_q[0]), .B(Counter_q[1]), .C(Counter_q[2]), .D(Counter_q[3]), .Q(kOut));
  Register _1s (.D(adder_2_out), .en(kOut), .Q(_1s_q), .clk(CLK));  // open: clr
  Register _0s (.D(adder_3_out), .en(not_1_out), .Q(_0s_q), .clk(CLK));  // open: clr
  not not_1 (not_1_out, kOut);
  Adder adder_2 (.a(_1s_q), .b(8'h1), .out(adder_2_out));  // open: cin, cout
  Adder adder_3 (.a(_0s_q), .b(8'h1), .out(adder_3_out));  // open: cin, cout

  // Notes on the sheet:
  //   Zachary Whitney Lab 6
  //   CS 447 MWF 11AM
endmodule

module kmap (
  input  A,
  input  B,
  input  C,
  input  D,
  output Q
);

  wire and_1_out, and_2_out, and_3_out, and_4_out;

  and and_1 (and_1_out, ~A, ~C);  // AND_Gate
  and and_2 (and_2_out, ~C, ~B);  // AND_Gate
  and and_3 (and_3_out, ~D, ~B);  // AND_Gate
  and and_4 (and_4_out, B, D);
  or or_1 (Q, and_1_out, and_2_out, and_3_out, and_4_out);
endmodule
