// Logisim project zdw9_lab7.circ as structural Verilog: 2 circuits, main circuit main
module main (
);

  wire Add, and_1_out, button_1_out, CLK, clock_1_out, Done, not_1_out, not_2_out, not_3_out;
  wire [7:0] bIn, bOut;
  wire [15:0] adder_1_out, aIn, aOut, cOut;

  Clock clock_1 (.out(clock_1_out));
  or or_1 (CLK, clock_1_out, button_1_out);
  Button button_1 (.out(button_1_out));
  LED u_Done (.in(Done));
  not not_1 (not_1_out, Done);
  Register #(.width(16)) Multiplicand (.D(aOut), .en(not_1_out), .Q(aIn), .clk(CLK));  // open: clr
  Shifter #(.width(16)) shifter_1 (.in(aIn), .\dist (4'b0001), .out(aOut));
  // Probe on cOut
  not not_2 (not_2_out, Done);
  Shifter #(.shift("lr")) shifter_2 (.in(bIn), .\dist (3'b001), .out(bOut));
  Comparator comparator_1 (.a(bIn), .b({8{1'b0}}), .eq(Done));  // open: gt, lt
  Register Multiplier (.D(bOut), .en(not_2_out), .Q(bIn), .clk(CLK));  // open: clr
  Adder #(.width(16)) adder_1 (.a(cOut), .b(aIn), .out(adder_1_out));  // open: cin, cout
  not not_3 (not_3_out, Done);
  Register #(.width(16)) Product (.D(adder_1_out), .en(and_1_out), .Q(cOut), .clk(CLK));  // open: clr
  and and_1 (and_1_out, Add, not_3_out);
  Comparator #(.width(1)) comparator_2 (.a(bIn[0]), .b(1'b1), .eq(Add));  // open: gt, lt

  // Notes on the sheet:
  //   Zachary Whitney Lab 7
  //   CS 447 MWF 11AM
endmodule

module Division (
);

  wire button_1_out, CLK, clock_1_out, comparator_1_eq, comparator_1_lt, Done, fits, not_1_out, not_2_out;
  wire [3:0] Counter_q;
  wire [7:0] or_3_out, qIn, qOut, shiftedQ;
  wire [15:0] divOut, rdIn, rdOut, shiftedRD, shifter_2_out, subtractor_1_out;

  Clock clock_1 (.out(clock_1_out));
  or or_1 (CLK, clock_1_out, button_1_out);
  Button button_1 (.out(button_1_out));
  LED u_Done (.in(Done));
  not not_1 (not_1_out, Done);
  Register #(.width(16)) Remainder_Dividend (.D(rdIn), .en(not_1_out), .Q(rdOut), .clk(CLK));  // open: clr
  Shifter #(.width(16)) shifter_1 (.in(rdOut), .\dist (4'b0001), .out(shiftedRD));
  Subtractor #(.width(16)) subtractor_1 (.a(shiftedRD), .b(shifter_2_out), .out(subtractor_1_out));  // open: bin, bout
  Shifter #(.width(16)) shifter_2 (.in(divOut), .\dist (4'b1000), .out(shifter_2_out));
  // Probe on qOut
  Counter #(.width(4), .max('h8), .ongoal("stay")) Counter (
    .Q(Counter_q), .clk(CLK));  // open: load, D, count, carry, clr
  Multiplexer #(.width(16), .enable("false")) multiplexer_1 (
    .in0(shiftedRD), .in1(subtractor_1_out), .out(rdIn), .sel(fits));
  Register #(.width(16)) Divisor (.Q(divOut), .clk(CLK));  // open: D, en, clr
  or or_2 (fits, comparator_1_eq, comparator_1_lt);
  Comparator #(.mode("unsigned")) comparator_1 (
    .a(divOut[7:0]), .b(shiftedRD[15:8]), .eq(comparator_1_eq), .lt(comparator_1_lt));  // open: gt
  Comparator #(.width(4), .mode("unsigned")) comparator_2 (.a(Counter_q), .b(4'b1000), .eq(Done));  // open: gt, lt
  not not_2 (not_2_out, Done);
  assign or_3_out = shiftedQ | 8'h1;  // OR_Gate or_3, 8 bits wide
  Register Quotient (.D(qIn), .en(not_2_out), .Q(qOut), .clk(CLK));  // open: clr
  Shifter shifter_3 (.in(qOut), .\dist (3'b001), .out(shiftedQ));
  Multiplexer #(.width(8), .enable("false")) multiplexer_2 (.in0(shiftedQ), .in1(or_3_out), .out(qIn), .sel(fits));

  // Notes on the sheet:
  //   CS 447 MWF 11AM
  //   Zachary Whitney Lab 7
endmodule
