// Logisim project zdw9_lab8.circ as structural Verilog: 2 circuits, main circuit main
module main (
);

  Register_File register_file_1 ();  // open: CLK, DATA, WE, incr7, decr7, rd, rs, rt, rt_out, rs_out
endmodule

module Register_File (
  input  CLK,
  input  [15:0] DATA,
  input  WE,
  input  incr7,
  input  decr7,
  input  [2:0] rd,
  input  [2:0] rs,
  input  [2:0] rt,
  output [15:0] rt_out,
  output [15:0] rs_out
);

  wire _0e, _1e, _2e, _3e, _4e, _5e, _6e, _7e, adj, or_2_out;
  wire [15:0] adder_1_out, multiplexer_3_out, r0out, r1out, r2out, r3out, r4out, r5out, r6out, r7in, r7out,
       r7temp, subtractor_1_out;

  Register #(.width(16)) r0 (.D(DATA), .en(_0e), .Q(r0out), .clk(CLK));  // open: clr
  Register #(.width(16)) r4 (.D(DATA), .en(_4e), .Q(r4out), .clk(CLK));  // open: clr
  Register #(.width(16)) r1 (.D(DATA), .en(_1e), .Q(r1out), .clk(CLK));  // open: clr
  Register #(.width(16)) r5 (.D(DATA), .en(_5e), .Q(r5out), .clk(CLK));  // open: clr
  Multiplexer #(.select(3), .width(16), .enable("false")) multiplexer_1 (
    .in0(r0out), .in1(r1out), .in2(r2out), .in3(r3out), .in4(r4out), .in5(r5out), .in6(r6out), .in7(r7out),
    .out(rt_out), .sel(rt));
  or or_1 (adj, decr7, incr7);
  Register #(.width(16)) r2 (.D(DATA), .en(_2e), .Q(r2out), .clk(CLK));  // open: clr
  Register #(.width(16)) r6 (.D(DATA), .en(_6e), .Q(r6out), .clk(CLK));  // open: clr
  Multiplexer #(.select(3), .width(16), .enable("false")) multiplexer_2 (
    .in0(r0out), .in1(r1out), .in2(r2out), .in3(r3out), .in4(r4out), .in5(r5out), .in6(r6out), .in7(r7out),
    .out(rs_out), .sel(rs));
  Register #(.width(16)) r3 (.D(DATA), .en(_3e), .Q(r3out), .clk(CLK));  // open: clr
  Demultiplexer #(.select(3), .enable("false")) demultiplexer_1 (
    .out0(_0e), .out1(_1e), .out2(_2e), .out3(_3e), .out4(_4e), .out5(_5e), .out6(_6e), .out7(_7e), .in(WE),
    .sel(rd));
  Multiplexer #(.width(16), .enable("false")) multiplexer_3 (
    .in0(DATA), .in1(r7in), .out(multiplexer_3_out), .sel(adj));
  Register #(.width(16)) r7 (.D(multiplexer_3_out), .en(or_2_out), .Q(r7temp), .clk(CLK));  // open: clr
  or or_2 (or_2_out, _7e, incr7, decr7);
  Subtractor #(.width(16)) subtractor_1 (.a(r7temp), .b(16'h1), .out(subtractor_1_out));  // open: bin, bout
  Adder #(.width(16)) adder_1 (.a(r7out), .b(16'h1), .out(adder_1_out));  // open: cin, cout
  Multiplexer #(.width(16), .enable("false")) multiplexer_4 (
    .in0(r7temp), .in1(subtractor_1_out), .out(r7out), .sel(decr7));
  Multiplexer #(.width(16), .enable("false")) multiplexer_5 (.in0(r7out), .in1(adder_1_out), .out(r7in), .sel(incr7));

  // Notes on the sheet:
  //   Zachary Whitney zdw9
  //   Lab 8 CS 447 MWF 11AM
endmodule
